// Logisim project 8bit_adder.circ as structural Verilog: 1 circuit, main circuit 8bit_adder
// ADD
module _8bit_adder (
  input  X7,
  input  X6,
  input  X5,
  input  X4,
  input  X3,
  input  X2,
  input  X1,
  input  X0,
  input  Y7,
  input  Y6,
  input  Y5,
  input  Y4,
  input  Y3,
  input  Y2,
  input  Y1,
  input  Y0,
  output O0,
  output O1,
  output O2,
  output O3,
  output O4,
  output O5,
  output O6,
  output O7
);

  wire full_adder_1_so0, full_adder_2_so0, full_adder_3_so0, full_adder_4_so0, full_adder_5_so0,
       full_adder_6_so0, full_adder_8_so0;

  full_adder full_adder_1 (.X0(X0), .Y0(Y0), .Si0(1'b0), .O0(O0), .So0(full_adder_1_so0));
  full_adder full_adder_2 (.X0(X1), .Y0(Y1), .Si0(full_adder_1_so0), .O0(O1), .So0(full_adder_2_so0));
  full_adder full_adder_3 (.X0(X2), .Y0(Y2), .Si0(full_adder_2_so0), .O0(O2), .So0(full_adder_3_so0));
  full_adder full_adder_4 (.X0(X3), .Y0(Y3), .Si0(full_adder_3_so0), .O0(O3), .So0(full_adder_4_so0));
  full_adder full_adder_5 (.X0(X4), .Y0(Y4), .Si0(full_adder_4_so0), .O0(O4), .So0(full_adder_5_so0));
  full_adder full_adder_6 (.X0(X5), .Y0(Y5), .Si0(full_adder_5_so0), .O0(O5), .So0(full_adder_6_so0));
  full_adder full_adder_7 (.X0(X7), .Y0(Y7), .Si0(full_adder_8_so0), .O0(O7));  // open: So0
  full_adder full_adder_8 (.X0(X6), .Y0(Y6), .Si0(full_adder_6_so0), .O0(O6), .So0(full_adder_8_so0));
endmodule
