// Logisim project full_adder.circ as structural Verilog: 1 circuit, main circuit full_adder
// ADD
module full_adder (
  input  X0,
  input  Y0,
  input  Si0,
  output O0,
  output So0
);

  wire and_1_out, and_2_out, xor_1_out;

  xor xor_1 (xor_1_out, X0, Y0);
  and and_1 (and_1_out, X0, Y0);
  and and_2 (and_2_out, xor_1_out, Si0);
  xor xor_2 (O0, xor_1_out, Si0);
  or or_1 (So0, and_2_out, and_1_out);
endmodule
